// Logisim project cpu.circ as structural Verilog: 3 circuits, main circuit main
module main (
);

  wire clock, decoder_1_out1, decoder_1_out9, decoder_1_out10, not_1_out, reset;
  wire [6:0] bit_extender_1_out;
  wire [7:0] adder_1_out, multiplexer_1_out, multiplexer_2_out, multiplexer_3_out, PC_q,
       registerfile_1_outreg2;
  wire [15:0] rom_1_data;

  Button button_1 (.out(reset));
  Clock clock_1 (.out(clock));
  // Probe on multiplexer_1_out
  Register PC (.D(multiplexer_1_out), .en(clock), .clk(clock), .Q(PC_q), .clr(reset));
  not not_1 (not_1_out, decoder_1_out9);
  Multiplexer #(.enable("false"), .width(8)) multiplexer_1 (
    .in0(registerfile_1_outreg2), .in1(adder_1_out), .out(multiplexer_1_out), .sel(not_1_out));
  Adder adder_1 (.a(8'h1), .b(PC_q), .out(adder_1_out));  // open: cin, cout
  ROM #(.dataWidth(16)) rom_1 (.addr(PC_q), .data(rom_1_data));
  // Probe on adder_1_out
  // Probe on rom_1_data
  Decoder #(.enable("false"), .select(4)) decoder_1 (
    .out1(decoder_1_out1), .out9(decoder_1_out9), .out10(decoder_1_out10), .sel(rom_1_data[15:12]));  // open: out0, out2, out3, out4, out5, out6, out7, out8, out11, out12, out13, out14, out15
  Multiplexer #(.enable("false"), .width(8)) multiplexer_2 (
    .in1(rom_1_data[7:0]), .out(multiplexer_2_out), .sel(decoder_1_out1));  // open: in0
  // Probe on multiplexer_2_out
  Multiplexer #(.enable("false"), .width(8)) multiplexer_3 (
    .in0({8{1'b0}}), .in1(registerfile_1_outreg2), .out(multiplexer_3_out), .sel(decoder_1_out10));
  // Probe on registerfile_1_outreg2
  Bit_Extender #(.out_width(7)) bit_extender_1 (.in(multiplexer_3_out), .out(bit_extender_1_out));
  RegisterFile registerfile_1 (
    .WriteData(multiplexer_2_out), .WriteReg(rom_1_data[10:8]), .ReadReg1(rom_1_data[10:8]),
    .WriteEnable(rom_1_data[11]), .ReadReg2(rom_1_data[2:0]), .clock(clock), .Clear(reset),
    .OutReg2(registerfile_1_outreg2));  // open: OutReg1
  TTY tty_1 (.data(bit_extender_1_out), .clk(clock), .clr(reset));  // open: we

  // Notes on the sheet:
  //   contents of rom_1 (hex, n*v repeats v):
  //   1848 a008 1845 a008 184c a008 184c a008 184f a008 180a a008 1800 9080 5*100
endmodule

module RegisterFile (
  input  [7:0] WriteData,
  input  [2:0] WriteReg,
  input  [2:0] ReadReg1,
  input  WriteEnable,
  input  [2:0] ReadReg2,
  input  clock,
  input  Clear,
  output [7:0] OutReg1,
  output [7:0] OutReg2
);

  wire decoder_1_out0, decoder_1_out1, decoder_1_out2, decoder_1_out3, decoder_1_out4, decoder_1_out5,
       decoder_1_out6, decoder_1_out7;
  wire [7:0] register_1_q, register_2_q, register_3_q, register_4_q, register_5_q, register_6_q,
       register_7_q, register_8_q;

  Decoder #(.select(3)) decoder_1 (
    .out0(decoder_1_out0), .out1(decoder_1_out1), .out2(decoder_1_out2), .out3(decoder_1_out3),
    .out4(decoder_1_out4), .out5(decoder_1_out5), .out6(decoder_1_out6), .out7(decoder_1_out7),
    .sel(WriteReg), .en(WriteEnable));
  Register #(.trigger("falling")) register_1 (
    .D(WriteData), .en(decoder_1_out0), .clk(clock), .Q(register_1_q), .clr(Clear));
  Register #(.trigger("falling")) register_2 (
    .D(WriteData), .en(decoder_1_out1), .clk(clock), .Q(register_2_q), .clr(Clear));
  Register #(.trigger("falling")) register_3 (
    .D(WriteData), .en(decoder_1_out2), .clk(clock), .Q(register_3_q), .clr(Clear));
  Register #(.trigger("falling")) register_4 (
    .D(WriteData), .en(decoder_1_out3), .clk(clock), .Q(register_4_q), .clr(Clear));
  Register #(.trigger("falling")) register_5 (
    .D(WriteData), .en(decoder_1_out4), .clk(clock), .Q(register_5_q), .clr(Clear));
  Register #(.trigger("falling")) register_6 (
    .D(WriteData), .en(decoder_1_out5), .clk(clock), .Q(register_6_q), .clr(Clear));
  Register #(.trigger("falling")) register_7 (
    .D(WriteData), .en(decoder_1_out6), .clk(clock), .Q(register_7_q), .clr(Clear));
  Register #(.trigger("falling")) register_8 (
    .D(WriteData), .en(decoder_1_out7), .clk(clock), .Q(register_8_q), .clr(Clear));
  Multiplexer #(.enable("false"), .select(3), .width(8)) multiplexer_1 (
    .in0(register_1_q), .in1(register_2_q), .in2(register_3_q), .in3(register_4_q), .in4(register_5_q),
    .in5(register_6_q), .in6(register_7_q), .in7(register_8_q), .out(OutReg1), .sel(ReadReg2));
  Multiplexer #(.enable("false"), .select(3), .width(8)) multiplexer_2 (
    .in0(register_1_q), .in1(register_2_q), .in2(register_3_q), .in3(register_4_q), .in4(register_5_q),
    .in5(register_6_q), .in6(register_7_q), .in7(register_8_q), .out(OutReg2), .sel(ReadReg1));
endmodule

module TestTestRegisterFiule (
  input  [15:0] in_1,
  input  [2:0] in_2,
  input  [2:0] in_3,
  input  in_4,
  input  [2:0] in_5,
  output [15:0] out_6,
  output [15:0] out_7
);

  wire clock_1_out;

  Clock clock_1 (.out(clock_1_out));
  // RegisterFile registerfile_1: pin names not known; wires that end beside it: in_1, in_2, in_3, in_4, in_5, clock_1_out, out_6, out_7
endmodule
